// Logisim project lab7.circ as structural Verilog: 1 circuit, main circuit main
module main (
  input  [1:0] OPCODE,
  input  S2,
  input  [31:0] Source2,
  input  in_4,
  input  in_5,
  input  WE,
  input  [1:0] Sw,
  input  [1:0] Sr0,
  input  [1:0] Sr1,
  input  [31:0] Source0,
  input  [31:0] Source1
);

  wire clock_1_out, comparator_1_eq, demultiplexer_1_out0, demultiplexer_1_out1, demultiplexer_1_out2,
       demultiplexer_1_out3, not_1_out;
  wire [31:0] adder_1_out, and_1_out, multiplexer_1_out, multiplexer_2_out, multiplexer_3_out,
       multiplexer_4_out, multiplexer_5_out, multiplexer_6_out, or_1_out, R0_q, R1_q, R2_q, R3_q, xnor_1_out;

  Multiplexer #(.width(32)) multiplexer_1 (.in0(Source0), .in1(multiplexer_5_out), .out(multiplexer_1_out), .sel(in_5));
  Multiplexer #(.width(32)) multiplexer_2 (.in0(Source1), .in1(multiplexer_6_out), .out(multiplexer_2_out), .sel(in_4));
  assign or_1_out = multiplexer_1_out | multiplexer_2_out;  // OR_Gate or_1, 32 bits wide
  Adder #(.width(32)) adder_1 (.a(multiplexer_1_out), .b(multiplexer_2_out), .out(adder_1_out));  // open: cin, cout
  assign and_1_out = multiplexer_1_out & multiplexer_2_out;  // AND_Gate and_1, 32 bits wide
  assign xnor_1_out = ~(multiplexer_1_out ^ multiplexer_2_out);  // XNOR_Gate xnor_1, 32 bits wide
  Multiplexer #(.select(2), .width(32)) multiplexer_3 (
    .in0(or_1_out), .in1(adder_1_out), .in2(and_1_out), .in3(xnor_1_out), .out(multiplexer_3_out),
    .sel(OPCODE));
  Comparator #(.width(32)) comparator_1 (.a({32{1'b1}}), .b(multiplexer_3_out), .eq(comparator_1_eq));  // open: gt, lt
  not not_1 (not_1_out, comparator_1_eq);
  LED led_1 (.in(not_1_out));
  Multiplexer #(.width(32)) multiplexer_4 (.in0(multiplexer_3_out), .in1(Source2), .out(multiplexer_4_out), .sel(S2));
  Demultiplexer #(.select(2)) demultiplexer_1 (
    .out0(demultiplexer_1_out0), .out1(demultiplexer_1_out1), .out2(demultiplexer_1_out2),
    .out3(demultiplexer_1_out3), .in(WE), .sel(Sw));
  Clock clock_1 (.out(clock_1_out));
  Register #(.width(32)) R0 (
    .D(multiplexer_4_out), .en(demultiplexer_1_out0), .clk(clock_1_out), .Q(R0_q));  // open: clr
  Register #(.width(32)) R1 (
    .D(multiplexer_4_out), .en(demultiplexer_1_out1), .clk(clock_1_out), .Q(R1_q));  // open: clr
  Register #(.width(32)) R2 (
    .D(multiplexer_4_out), .en(demultiplexer_1_out2), .clk(clock_1_out), .Q(R2_q));  // open: clr
  Register #(.width(32)) R3 (
    .D(multiplexer_4_out), .en(demultiplexer_1_out3), .clk(clock_1_out), .Q(R3_q));  // open: clr
  Multiplexer #(.select(2), .width(32)) multiplexer_5 (
    .in0(R0_q), .in1(R1_q), .in2(R2_q), .in3(R3_q), .out(multiplexer_5_out), .sel(Sr0));
  Multiplexer #(.select(2), .width(32)) multiplexer_6 (
    .in0(R0_q), .in1(R1_q), .in2(R2_q), .in3(R3_q), .out(multiplexer_6_out), .sel(Sr1));

  // Notes on the sheet:
  //   ALU
  //   Register File
endmodule
